# Fritzing sketch kiln_control (saved by Fritzing 0.9.3b)
perfboards: 1
stripboards: 1

parts:
  J1 = female pin header, 8 pins [form="♀ (female)"]
  J2 = female pin header, 8 pins [form="♀ (female)"]
  J3 = male pin header, 8 pins [form="♂ (male)"]
  J4 = male pin header, 8 pins [form="♂ (male)"]
  J5 = double row male pin header, 6 pins [form="♂ (male)"]  # not connected
  J6 = Camdenboss CTB0158-2 [part_number=CTB0158-2 package=THT]  # not connected
  S1 = SWITCH-MOMENTARY-2 [package=tactile_switch_tall]
  R2 = Resistor [tolerance=±5% resistance=4.7k package=THT]
  J7 = female pin header, 5 pins [form="♀ (female)"]
  X1 = USB Connectors [package=usb-microb]
  U1 = mystery part, 3 pins [chip_label=AMS1117]
  U1_2 = mystery part, 3 pins [chip_label=AMS1117]
  DS1 = DS18B20 1-Wire Temperature Sensor [part_number=DS18B20]
  R3 = Resistor [tolerance=±5% resistance=4.7k package=THT]
  J8 = female pin header, 6 pins [form="♀ (female)"]
  J9 = Screw terminal - 2 pins [package=THT]
  J10 = female pin header, 18 pins [form="♀ (female)"]  # not connected

nets:
  N1: J1.pin1, J3.pin1
  N2: J1.pin2, J3.pin2
  N3: J1.pin3, J3.pin3, S1.2, R2.Pin_0
  N4: J1.pin4, J3.pin4, DS1.DQ, R3.Pin_1
  N5: J1.pin5, J3.pin5
  N6: J1.pin6, J3.pin6
  N7: J1.pin7, J3.pin7
  N8: J1.pin8, J3.pin8, J7.pin1, U1.pin1, U1_2.pin1, DS1.GND, J8.pin3, J9.pin2
  N9: J2.pin1, J4.pin1
  N10: J2.pin2, J4.pin2
  N11: J2.pin3, J4.pin3
  N12: J2.pin4, J4.pin4, J9.pin1
  N13: J2.pin5, J4.pin5, J8.pin6
  N14: J2.pin6, J4.pin6, J8.pin5
  N15: J2.pin7, J4.pin7, J8.pin4
  N16: J2.pin8, J4.pin8, R2.Pin_1, U1.pin2, U1_2.pin2, DS1.VDD, R3.Pin_0, J8.pin2
  N17: J7.pin2, X1.GND
  N18: J7.pin4, X1.VBUS
  N19: J7.pin5, U1.pin3, U1_2.pin3

notes:
  CS
  V3.3
  MAX31855
  CLK
  D0
  GND
  5V
  GPIO14 -> CLK
  GPIO12 -> CS
  GPIO13 -> D0
  GPIO16 -> SSR
  20 Löcher
  18 Löcher
  3.3V
  DO
